// Logisim project 2bit_fa.circ as structural Verilog: 1 circuit, main circuit main
module main (
  input  K1,
  input  A,
  input  B,
  input  Cin,
  input  K2,
  input  K3,
  output S,
  output Cout
);

  wire and_1_out, and_2_out, Key_1_out, Key_2_out, Key_3_out, not_1_out, xor_1_out;

  xor xor_1 (xor_1_out, A, B);
  and and_1 (and_1_out, A, B);
  xor Key_1 (Key_1_out, K1, xor_1_out);
  xor xor_2 (S, Key_1_out, Cin);
  and and_2 (and_2_out, Key_1_out, Cin);
  xor Key_2 (Key_2_out, and_2_out, K2);
  not not_1 (not_1_out, Key_2_out);
  xor Key_3 (Key_3_out, and_1_out, K3);
  or or_1 (Cout, not_1_out, Key_3_out);

  // Notes on the sheet:
  //   1
  //   2
  //   3
  //   4
  //   5
  //   6
  //   7
  //   8
  //   9
  //   10
  //   11
  //   12
  //   13
  //   14
  //   16
endmodule
