// Logisim project FA_2.circ as structural Verilog: 1 circuit, main circuit main
module main (
  input  A0,
  input  B0,
  input  Cin,
  input  A1,
  input  B1,
  output S0,
  output S1,
  output Cout
);

  wire and_1_out, and_2_out, and_3_out, and_4_out, or_1_out, xor_1_out, xor_2_out;

  xor xor_1 (xor_1_out, A0, B0);
  and and_1 (and_1_out, A0, B0);
  xor xor_2 (xor_2_out, A1, B1);
  and and_2 (and_2_out, A1, B1);
  xor xor_3 (S0, xor_1_out, Cin);
  and and_3 (and_3_out, xor_1_out, Cin);
  xor xor_4 (S1, xor_2_out, or_1_out);
  and and_4 (and_4_out, xor_2_out, or_1_out);
  or or_1 (or_1_out, and_3_out, and_1_out);
  or or_2 (Cout, and_4_out, and_2_out);

  // Notes on the sheet:
  //   1
  //   2
  //   3
  //   17
  //   18
  //   19
  //   4
  //   5
  //   6
  //   7
  //   20
  //   21
  //   22
  //   23
  //   8
  //   9
  //   24
  //   25
  //   10
  //   11
  //   12
  //   13
  //   26
  //   27
  //   28
  //   29
  //   14
  //   15
  //   30
  //   31
  //   16
  //   32
endmodule
