// Logisim project FA_3.circ as structural Verilog: 1 circuit, main circuit main
module main (
  input  A0,
  input  B0,
  input  Cin,
  input  A1,
  input  B1,
  input  A2,
  input  B2,
  output S0,
  output S1,
  output S2,
  output Cout
);

  wire and_1_out, and_2_out, and_3_out, and_4_out, and_5_out, and_6_out, or_1_out, or_2_out, xor_1_out,
       xor_2_out, xor_3_out;

  xor xor_1 (xor_1_out, A0, B0);
  and and_1 (and_1_out, A0, B0);
  xor xor_2 (xor_2_out, A1, B1);
  and and_2 (and_2_out, A1, B1);
  xor xor_3 (xor_3_out, A2, B2);
  and and_3 (and_3_out, A2, B2);
  and and_4 (and_4_out, xor_1_out, Cin);
  xor xor_4 (S0, xor_1_out, Cin);
  xor xor_5 (S1, xor_2_out, or_1_out);
  and and_5 (and_5_out, xor_2_out, or_1_out);
  xor xor_6 (S2, xor_3_out, or_2_out);
  and and_6 (and_6_out, xor_3_out, or_2_out);
  or or_1 (or_1_out, and_4_out, and_1_out);
  or or_2 (or_2_out, and_5_out, and_2_out);
  or or_3 (Cout, and_6_out, and_3_out);

  // Notes on the sheet:
  //   1
  //   2
  //   3
  //   17
  //   18
  //   19
  //   33
  //   34
  //   35
  //   4
  //   5
  //   6
  //   7
  //   20
  //   21
  //   22
  //   23
  //   36
  //   37
  //   38
  //   39
  //   8
  //   9
  //   24
  //   25
  //   40
  //   41
  //   10
  //   11
  //   12
  //   13
  //   26
  //   27
  //   28
  //   29
  //   42
  //   43
  //   44
  //   45
  //   14
  //   15
  //   30
  //   31
  //   46
  //   47
  //   16
  //   32
  //   48
endmodule
