// Logisim project FA_encrypt.circ as structural Verilog: 1 circuit, main circuit main
module main (
  input  SW13,
  input  A,
  input  SW15,
  input  in_4,
  input  B,
  input  SW14,
  input  Cin,
  output S,
  output Cout
);

  wire and_1_out, and_2_out, Key_1_out, Key_3_out, multiplexer_1_out, not_1_out, xor_1_out;

  xor xor_1 (xor_1_out, A, B);
  and and_1 (and_1_out, A, B);
  xor Key_1 (Key_1_out, SW13, xor_1_out);
  not not_1 (not_1_out, SW15);
  xor Key_3 (Key_3_out, not_1_out, Cin);
  xor xor_2 (S, Key_1_out, Key_3_out);
  and and_2 (and_2_out, Key_1_out, Cin);
  Multiplexer multiplexer_1 (.in0(in_4), .in1(and_2_out), .out(multiplexer_1_out), .sel(SW14));  // open: en
  or or_1 (Cout, multiplexer_1_out, and_1_out);

  // Notes on the sheet:
  //   1
  //   2
  //   3
  //   4
  //   5
  //   6
  //   7
  //   8
  //   9
  //   10
  //   11
  //   12
  //   13
  //   14
  //   15
  //   16
endmodule
