// Logisim project 6bit_fa_encrypted.circ as structural Verilog: 1 circuit, main circuit main
module main (
  input  K1,
  input  A,
  input  B,
  input  Cin,
  input  K2,
  input  K3,
  input  K4,
  input  A1,
  input  B1,
  input  K5,
  input  K6,
  input  K7,
  input  A2,
  input  B2,
  input  K8,
  input  K9,
  output S,
  output S1,
  output S2,
  output Cout
);

  wire and_1_out, and_2_out, and_3_out, and_4_out, and_5_out, and_6_out, Key_1_out, Key_2_out, Key_3_2_out,
       Key_3_out, Key_4_out, Key_5_out, Key_6_out, Key_8_out, Key_9_out, or_1_out, or_2_out, xor_1_out,
       xor_2_out, xor_3_out;

  xor xor_1 (xor_1_out, A, B);
  and and_1 (and_1_out, A, B);
  xor xor_2 (xor_2_out, A1, B1);
  and and_2 (and_2_out, A1, B1);
  xor xor_3 (xor_3_out, A2, B2);
  and and_3 (and_3_out, A2, B2);
  xnor Key_1 (Key_1_out, K1, xor_1_out);
  xor Key_4 (Key_4_out, K4, xor_2_out);
  xor Key_3 (Key_3_out, K7, xor_3_out);
  xor xor_4 (S, Key_1_out, Cin);
  and and_4 (and_4_out, Key_1_out, Cin);
  xor xor_5 (S1, Key_4_out, or_1_out);
  and and_5 (and_5_out, Key_4_out, or_1_out);
  xor xor_6 (S2, Key_3_out, or_2_out);
  and and_6 (and_6_out, Key_3_out, or_2_out);
  xor Key_2 (Key_2_out, and_4_out, K2);
  xor Key_3_2 (Key_3_2_out, and_1_out, K3);
  xnor Key_5 (Key_5_out, and_5_out, K5);
  xnor Key_6 (Key_6_out, and_2_out, K6);
  xor Key_8 (Key_8_out, and_6_out, K8);
  xor Key_9 (Key_9_out, and_3_out, K9);
  or or_1 (or_1_out, Key_2_out, Key_3_2_out);
  or or_2 (or_2_out, Key_5_out, Key_6_out);
  or or_3 (Cout, Key_8_out, Key_9_out);

  // Notes on the sheet:
  //   1
  //   2
  //   3
  //   4
  //   5
  //   6
  //   7
  //   8
  //   9
  //   10
  //   11
  //   12
  //   13
  //   14
  //   15
  //   16
endmodule
