// Logisim project FA_encrypt_new.circ as structural Verilog: 1 circuit, main circuit main
module main (
  input  SW15,
  input  A,
  input  B,
  input  Cin,
  input  SW14,
  output S,
  output Cout
);

  wire AND1_out, AND2_out, Key_1_out, Key_2_out, XOR1_out;

  xor XOR1 (XOR1_out, A, B);
  and AND1 (AND1_out, A, B);
  xnor Key_2 (Key_2_out, AND1_out, SW14);
  xor Key_1 (Key_1_out, SW15, XOR1_out);
  xor XOR2 (S, Key_1_out, Cin);
  and AND2 (AND2_out, XOR1_out, Cin);
  or OR1 (Cout, AND2_out, Key_2_out);

  // Notes on the sheet:
  //   1
  //   2
  //   3
  //   4
  //   5
  //   6
  //   7
  //   8
  //   9
  //   10
  //   11
  //   12
  //   13
  //   14
  //   15
  //   16
endmodule
